# Fritzing sketch circuit (saved by Fritzing 0.8.7b)
breadboards: 1

parts:
  V1 = DC Power [voltage=3.7]
  V2 = DC Power [voltage=3.7]
  Arduino = Arduino Nano (Rev3.0)
  R2 = Resistor [tolerance=±5% resistance=10k package=THT]
  L1 = Inductor [package="400 mil [THT]"]
  S3 = Pushbutton [package=THT]
  D2 = Rectifier Diode [part_number=FMG-G2CS-ND package="300 mil [THT]"]
  R4 = Resistor [tolerance=±5% resistance=10M package=THT]
  R5 = Resistor [tolerance=±5% resistance=10M package=THT]
  R7 = Resistor [tolerance=±5% resistance=10k package=THT]
  Q3 = Basic FET N-Channel [part_number=568-4897-5-ND package="TO220 [THT]"]
  R11 = Resistor [tolerance=±5% resistance=10k package=THT]
  S6 = Pushbutton [package=THT]
  R12 = Resistor [tolerance=±5% resistance=10k package=THT]
  S7 = Pushbutton [package=THT]

nets:
  N1: V1.V+, V2.V-
  GND: V1.V-, Arduino.GND, R2.Pin_1, R5.Pin_1, R7.Pin_1, Q3.source
  N2: V2.V+, Arduino.VIN, L1.pin_0, D2.cathode, R4.Pin_0
  N3: Arduino.D2, S3.leg1
  N4: Arduino.D9, S6.leg1
  N5: Arduino.D10, S7.leg1
  N6: Arduino.A2, R2.Pin_0, Q3.gate
  N7: Arduino.A1, R4.Pin_1, R5.Pin_0
  N8: L1.pin_1, D2.anode, Q3.drain
  N9: S3.leg0, R7.Pin_0
  N10: R11.Pin_0, S6.leg0
  N11: R12.Pin_0, S7.leg0

notes:
  screen SDA
  screen SCL
  screen
  read V
  read HR
  HR
  HR GND
  screen GND
  Main Power
  Vaporizing Coil
  Watts-
  Watts+
